// Digital circuit lab2_part2.dig as structural Verilog
module lab2_part2 (
  input  in0,
  input  in1,
  input  in2,
  input  in3,
  output seg_a,
  output seg_f,
  output seg_b,
  output seg_g,
  output seg_e,
  output seg_c,
  output seg_d,
  output seg_dp,
  output sign_a,
  output sign_f,
  output sign_b,
  output sign_g,
  output sign_e,
  output sign_c,
  output sign_d,
  output sign_dp
);

  wire and_1_out, and_2_out, and_3_out, and_4_out, and_5_out, and_6_out, and_7_out;

  Seven_Seg seven_seg_1 (.a(1'b0), .b(1'b0), .c(1'b0), .d(1'b0), .e(1'b0), .f(1'b0), .g(sign_g), .dp(1'b0));
  Seven_Seg seven_seg_2 (.a(seg_a), .b(seg_b), .c(seg_c), .d(seg_d), .e(seg_e), .f(seg_f), .g(seg_g), .dp(seg_dp));
  and and_1 (and_1_out, ~in0, in1, in2, in3);  // And
  and and_2 (and_2_out, in0, in1, ~in2, in3);  // And
  and and_3 (and_3_out, in0, in1, ~in2, ~in3);  // And
  and and_4 (and_4_out, ~in0, ~in1, ~in2, ~in3);  // And
  or or_1 (seg_a, and_1_out, and_2_out, and_3_out, and_4_out);
  and and_5 (and_5_out, ~in0, in1, ~in2, in3);  // And
  and and_6 (and_6_out, in0, ~in1, ~in2, in3);  // And
  and and_7 (and_7_out, in0, ~in1, in2, ~in3);  // And
  // Or or_2 has open pins: In_1=and_5_out, In_2=and_6_out, In_3=and_7_out, out=open

  assign sign_a = 1'b0;
  assign sign_b = 1'b0;
  assign sign_c = 1'b0;
  assign sign_d = 1'b0;
  assign sign_dp = 1'b0;
  assign sign_e = 1'b0;
  assign sign_f = 1'b0;

  // Notes on the sheet:
  //   Interface (do not edit the content inside this box)
  //   Outputs:
  //   Inputs
  //   Sign
  //   Decimal Number
endmodule

/* Test case:
in3 in2 in1 in0  sign_a sign_b sign_c sign_d sign_e sign_f sign_g  seg_a seg_b seg_c seg_d seg_e seg_f seg_g
 0   0   0   0    0      0      0      0      0      0      0       1     1     1     1     1     1     0
*/
